// Digital circuit 01_toolchain.dig as structural Verilog
module _01_toolchain (
  input  Reset,
  output [31:0] x1,
  output [31:0] x2,
  output [3:0] state,
  output [31:0] address,
  output [31:0] x3
);

  wire Clock_out;

  Button Clock (.out(Clock_out));
  maRVin #(.applicationType("IVERILOG"), .iverilogOptions("C:\\\\Users\\\\andre\\\\Downloads\\\\PROJECTS\\\\marvin\\\\rtl\\\\marvin_cpu.v\nC:\\\\Users\\\\andre\\\\Downloads\\\\PROJECTS\\\\marvin\\\\rtl\\\\marvin_mem.v"), .CodeFile("C:\\Users\\andre\\Downloads\\PROJECTS\\marvin\\rtl\\marvin.v")) u_maRVin (
    .clk(Clock_out), .nrst(Reset), .address(address), .dbg_x1(x1), .dbg_x2(x2), .dbg_x3(x3), .dbg_state(state));

  // Notes on the sheet:
  //   Reset: default 1
endmodule
