// Digital circuit 03_gpio_out.dig as structural Verilog
module _03_gpio_out (
  input  Reset,
  input  clk,
  output [31:0] x1,
  output [31:0] x2,
  output [31:0] address,
  output [31:0] x15
);

  wire [3:0] u_maRVin_gpio;

  maRVin #(.applicationType("IVERILOG"), .iverilogOptions("C:\\\\Users\\\\andre\\\\Downloads\\\\PROJECTS\\\\marvin\\\\rtl\\\\marvin_cpu.v\nC:\\\\Users\\\\andre\\\\Downloads\\\\PROJECTS\\\\marvin\\\\rtl\\\\marvin_mem.v\nC:\\\\Users\\\\andre\\\\Downloads\\\\PROJECTS\\\\marvin\\\\rtl\\\\marvin_gpio.v"), .CodeFile("C:\\Users\\andre\\Downloads\\PROJECTS\\marvin\\rtl\\marvin.v")) u_maRVin (
    .clk(clk), .nrst(Reset), .address(address), .dbg_x1(x1), .dbg_x2(x2), .dbg_x15(x15), .gpio(u_maRVin_gpio));
  LED led_1 (.in(u_maRVin_gpio[0]));
  LED led_2 (.in(u_maRVin_gpio[1]));
  LED led_3 (.in(u_maRVin_gpio[2]));
  LED led_4 (.in(u_maRVin_gpio[3]));

  // Notes on the sheet:
  //   Reset: default 1
  //   clk: Hz: 100
endmodule
