// Digital circuit 04_gpio_in.dig as structural Verilog
module _04_gpio_in (
  input  Reset,
  input  Clock,
  input  gpio_2,
  output [31:0] x1,
  output [31:0] x2,
  output [31:0] address,
  output [31:0] x15
);

  wire [1:0] u_maRVin_gpio_out;

  maRVin #(.applicationType("IVERILOG"), .iverilogOptions("C:\\\\Users\\\\andre\\\\Downloads\\\\PROJECTS\\\\marvin\\\\rtl\\\\marvin_cpu.v\nC:\\\\Users\\\\andre\\\\Downloads\\\\PROJECTS\\\\marvin\\\\rtl\\\\marvin_mem.v\nC:\\\\Users\\\\andre\\\\Downloads\\\\PROJECTS\\\\marvin\\\\rtl\\\\marvin_gpio.v"), .CodeFile("C:\\Users\\andre\\Downloads\\PROJECTS\\marvin\\rtl\\marvin.v")) u_maRVin (
    .clk(Clock), .nrst(Reset), .gpio_in(gpio_2), .address(address), .dbg_x1(x1), .dbg_x2(x2), .dbg_x15(x15),
    .gpio_out(u_maRVin_gpio_out));
  LED gpio_0 (.in(u_maRVin_gpio_out[0]));
  LED gpio_1 (.in(u_maRVin_gpio_out[1]));

  // Notes on the sheet:
  //   Reset: default 1
  //   Clock: Hz: 100
endmodule
