// Digital circuit 05_uart_tx.dig as structural Verilog
module _05_uart_tx (
  input  Reset,
  input  Clock,
  output [31:0] address
);

  wire u_maRVin_uart1_tx, u_uart_rx_wr;
  wire [7:0] u_uart_rx_data;
  wire [31:0] u_maRVin_gpio;

  maRVin #(.applicationType("IVERILOG"), .CodeFile("C:\\Users\\andre\\Downloads\\PROJECTS\\marvin\\rtl\\marvin.v")) u_maRVin (
    .clk(Clock), .nrst(Reset), .uart1_rx(1'b1), .address(address), .gpio(u_maRVin_gpio),
    .uart1_tx(u_maRVin_uart1_tx));
  uart_rx #(.applicationType("IVERILOG")) u_uart_rx (
    .clk(Clock), .rst_n(Reset), .rx(u_maRVin_uart1_tx), .data(u_uart_rx_data), .wr(u_uart_rx_wr));
  LED gpio_0 (.in(u_maRVin_gpio[0]));
  LED gpio_1 (.in(u_maRVin_gpio[1]));
  Terminal terminal_1 (.D(u_uart_rx_data), .C(u_uart_rx_wr), .en(1'b1));

  // Other names for the same wires on the sheet: clk = Clock; nrst = Reset

  // Notes on the sheet:
  //   Reset: default 1
  //   Clock: Hz: 1600
endmodule

/* Code of uart_rx:
// ============================================================
// uart_rx.v  -  Receptor UART 8N1 com oversampling 16x
// ------------------------------------------------------------
// Para uso como componente Verilog dentro do Digital (Neemann).
//
// Ligacao ao "Terminal" do Digital (Data / Clock / Enable):
//   data[7:0] -> Data  do Terminal
//   wr        -> Clock do Terminal   (pulso de 1 ciclo, borda de subida captura)
//   wr        -> Enable do Terminal  (ou fixe Enable = 1)
//
// Timing:
//   - Alimente 'clk' com o clock de sistema do Digital.
//   - Cada bit UART dura 16 bordas de 'clk' (oversampling 16x).
//   - Ou seja: baud_do_TX = frequencia_de_clk / 16.
//   - Dentro do Digital, aplique 16 pulsos de clock por bit transmitido.
//
// Frame: 1 start (0), 8 dados LSB-first, 1 stop (1). Sem paridade.
// Linha em repouso (idle) = 1.
// ============================================================

module uart_rx #(
    // Especifique a frequencia do clock e o baud rate.
    // O oversampling (clocks por bit) e calculado: OVS = CLK_FREQ / BAUD.
    // Ex.: CLK_FREQ = 1600, BAUD = 100  ->  OVS = 16.
    // No Digital, ajuste estes parametros na caixa do componente.
    // IMPORTANTE: CLK_FREQ deve ser multiplo inteiro de BAUD; caso
    // contrario ha arredondamento e o ponto de amostragem desloca.
    parameter CLK_FREQ = 1600,   // frequencia de 'clk' (Hz)
    parameter BAUD     = 100     // baud rate do TX (bps)
) (
    input  wire       clk,      // clock de sistema (CLK_FREQ Hz)
    input  wire       rst_n,    // reset sincrono, ativo em 0 (logica negativa)
    input  wire       rx,       // linha serial vinda do TX (idle = 1)
    output reg  [7:0] data,     // byte recebido -> Data do Terminal
    output reg        wr        // pulso 1 ciclo -> Clock/Enable do Terminal
);

    // Oversampling derivado: clocks de 'clk' por bit UART.
    localparam OVS = CLK_FREQ / BAUD;

    // Estados
    localparam ST_IDLE  = 2'd0;
    localparam ST_START = 2'd1;
    localparam ST_DATA  = 2'd2;
    localparam ST_STOP  = 2'd3;

    reg [1:0] state;
    reg [$clog2(OVS)-1:0] os_cnt;  // contador de oversampling (0..OVS-1)
    reg [2:0] bit_cnt;   // contador de bits de dados (0..7)
    reg [7:0] shreg;     // registrador de deslocamento

    // Sincronizador de entrada (2 flip-flops) contra metaestabilidade
    reg rx_s1, rx_s2;
    always @(posedge clk) begin
        rx_s1 <= rx;
        rx_s2 <= rx_s1;
    end
    wire rx_sync = rx_s2;

    always @(posedge clk) begin
        if (!rst_n) begin
            state   <= ST_IDLE;
            os_cnt  <= 0;
            bit_cnt <= 3'd0;
            shreg   <= 8'd0;
            data    <= 8'd0;
            wr      <= 1'b0;
        end else begin
            wr <= 1'b0;  // wr por padrao baixo; sobe so por 1 ciclo no fim

            case (state)
                // ------------------------------------------------
                ST_IDLE: begin
                    os_cnt  <= 0;
                    bit_cnt <= 3'd0;
                    // borda de descida = possivel start bit
                    if (rx_sync == 1'b0)
                        state <= ST_START;
                end

                // ------------------------------------------------
                // Espera ate o MEIO do start bit (8 amostras) e
                // confirma que ainda esta em 0 (start valido).
                ST_START: begin
                    if (os_cnt == (OVS/2 - 1)) begin
                        os_cnt <= 0;
                        if (rx_sync == 1'b0)
                            state <= ST_DATA;   // start confirmado
                        else
                            state <= ST_IDLE;   // ruido: aborta
                    end else begin
                        os_cnt <= os_cnt + 1'b1;
                    end
                end

                // ------------------------------------------------
                // Amostra cada bit de dado no seu centro:
                // 16 amostras apos o meio do start caimos no meio
                // de cada bit de dado.
                ST_DATA: begin
                    if (os_cnt == (OVS - 1)) begin
                        os_cnt <= 0;
                        shreg  <= {rx_sync, shreg[7:1]}; // LSB-first
                        if (bit_cnt == 3'd7)
                            state <= ST_STOP;
                        else
                            bit_cnt <= bit_cnt + 3'd1;
                    end else begin
                        os_cnt <= os_cnt + 1'b1;
                    end
                end

                // ------------------------------------------------
                // Centro do stop bit. Se = 1, byte valido -> pulso wr.
                // OBS: o Terminal do Digital trata tanto CR (0x0D) quanto
                // LF (0x0A) como quebra de linha. Enviar "\r\n" pularia
                // DUAS linhas. Por isso suprimimos o CR aqui: o pulso 'wr'
                // nao e gerado para 0x0D, deixando apenas o LF quebrar a
                // linha. (Se preferir manter o CR, remova o teste != 8'h0D.)
                ST_STOP: begin
                    if (os_cnt == (OVS - 1)) begin
                        os_cnt <= 0;
                        if (rx_sync == 1'b1 && shreg != 8'h0D) begin
                            data <= shreg;  // byte pronto
                            wr   <= 1'b1;   // pulso para o Terminal
                        end
                        state <= ST_IDLE;
                    end else begin
                        os_cnt <= os_cnt + 1'b1;
                    end
                end

                default: state <= ST_IDLE;
            endcase
        end
    end

endmodule
*/
