// Digital circuit 06_uart_rx.dig as structural Verilog
module _06_uart_rx (
  input  Reset,
  input  Clock,
  output [31:0] address
);

  wire keyboard_1_av, u_maRVin_uart1_tx, u_uart_rx_wr, u_uart_tx_next, u_uart_tx_tx;
  wire [7:0] u_uart_rx_data;
  wire [15:0] keyboard_1_d;
  wire [31:0] u_maRVin_gpio;

  uart_rx #(.applicationType("IVERILOG")) u_uart_rx (
    .clk(Clock), .rst_n(Reset), .rx(u_maRVin_uart1_tx), .data(u_uart_rx_data), .wr(u_uart_rx_wr));
  Keyboard keyboard_1 (.C(u_uart_tx_next), .en(1'b1), .D(keyboard_1_d), .av(keyboard_1_av));
  maRVin #(.applicationType("IVERILOG"), .CodeFile("C:\\Users\\andre\\Downloads\\PROJECTS\\marvin\\rtl\\marvin.v")) u_maRVin (
    .clk(Clock), .nrst(Reset), .uart1_rx(u_uart_tx_tx), .address(address), .gpio(u_maRVin_gpio),
    .uart1_tx(u_maRVin_uart1_tx));
  Terminal terminal_1 (.D(u_uart_rx_data), .C(u_uart_rx_wr), .en(1'b1));
  uart_tx #(.applicationType("IVERILOG")) u_uart_tx (
    .clk(Clock), .rst_n(Reset), .data(keyboard_1_d[7:0]), .av(keyboard_1_av), .tx(u_uart_tx_tx),
    .next(u_uart_tx_next));  // open: busy
  LED gpio_0 (.in(u_maRVin_gpio[0]));
  LED gpio_1 (.in(u_maRVin_gpio[1]));

  // Notes on the sheet:
  //   Reset: default 1
  //   Clock: Hz: 1600
endmodule

/* Code of uart_rx:
// ============================================================
// uart_rx.v  -  Receptor UART 8N1 com oversampling 16x
// ------------------------------------------------------------
// Para uso como componente Verilog dentro do Digital (Neemann).
//
// Ligacao ao "Terminal" do Digital (Data / Clock / Enable):
//   data[7:0] -> Data  do Terminal
//   wr        -> Clock do Terminal   (pulso de 1 ciclo, borda de subida captura)
//   wr        -> Enable do Terminal  (ou fixe Enable = 1)
//
// Timing:
//   - Alimente 'clk' com o clock de sistema do Digital.
//   - Cada bit UART dura 16 bordas de 'clk' (oversampling 16x).
//   - Ou seja: baud_do_TX = frequencia_de_clk / 16.
//   - Dentro do Digital, aplique 16 pulsos de clock por bit transmitido.
//
// Frame: 1 start (0), 8 dados LSB-first, 1 stop (1). Sem paridade.
// Linha em repouso (idle) = 1.
// ============================================================

module uart_rx #(
    // Especifique a frequencia do clock e o baud rate.
    // O oversampling (clocks por bit) e calculado: OVS = CLK_FREQ / BAUD.
    // Ex.: CLK_FREQ = 1600, BAUD = 100  ->  OVS = 16.
    // No Digital, ajuste estes parametros na caixa do componente.
    // IMPORTANTE: CLK_FREQ deve ser multiplo inteiro de BAUD; caso
    // contrario ha arredondamento e o ponto de amostragem desloca.
    parameter CLK_FREQ = 1600,   // frequencia de 'clk' (Hz)
    parameter BAUD     = 100     // baud rate do TX (bps)
) (
    input  wire       clk,      // clock de sistema (CLK_FREQ Hz)
    input  wire       rst_n,    // reset sincrono, ativo em 0 (logica negativa)
    input  wire       rx,       // linha serial vinda do TX (idle = 1)
    output reg  [7:0] data,     // byte recebido -> Data do Terminal
    output reg        wr        // pulso 1 ciclo -> Clock/Enable do Terminal
);

    // Oversampling derivado: clocks de 'clk' por bit UART.
    localparam OVS = CLK_FREQ / BAUD;

    // Estados
    localparam ST_IDLE  = 2'd0;
    localparam ST_START = 2'd1;
    localparam ST_DATA  = 2'd2;
    localparam ST_STOP  = 2'd3;

    reg [1:0] state;
    reg [$clog2(OVS)-1:0] os_cnt;  // contador de oversampling (0..OVS-1)
    reg [2:0] bit_cnt;   // contador de bits de dados (0..7)
    reg [7:0] shreg;     // registrador de deslocamento

    // Sincronizador de entrada (2 flip-flops) contra metaestabilidade
    reg rx_s1, rx_s2;
    always @(posedge clk) begin
        rx_s1 <= rx;
        rx_s2 <= rx_s1;
    end
    wire rx_sync = rx_s2;

    always @(posedge clk) begin
        if (!rst_n) begin
            state   <= ST_IDLE;
            os_cnt  <= 0;
            bit_cnt <= 3'd0;
            shreg   <= 8'd0;
            data    <= 8'd0;
            wr      <= 1'b0;
        end else begin
            wr <= 1'b0;  // wr por padrao baixo; sobe so por 1 ciclo no fim

            case (state)
                // ------------------------------------------------
                ST_IDLE: begin
                    os_cnt  <= 0;
                    bit_cnt <= 3'd0;
                    // borda de descida = possivel start bit
                    if (rx_sync == 1'b0)
                        state <= ST_START;
                end

                // ------------------------------------------------
                // Espera ate o MEIO do start bit (8 amostras) e
                // confirma que ainda esta em 0 (start valido).
                ST_START: begin
                    if (os_cnt == (OVS/2 - 1)) begin
                        os_cnt <= 0;
                        if (rx_sync == 1'b0)
                            state <= ST_DATA;   // start confirmado
                        else
                            state <= ST_IDLE;   // ruido: aborta
                    end else begin
                        os_cnt <= os_cnt + 1'b1;
                    end
                end

                // ------------------------------------------------
                // Amostra cada bit de dado no seu centro:
                // 16 amostras apos o meio do start caimos no meio
                // de cada bit de dado.
                ST_DATA: begin
                    if (os_cnt == (OVS - 1)) begin
                        os_cnt <= 0;
                        shreg  <= {rx_sync, shreg[7:1]}; // LSB-first
                        if (bit_cnt == 3'd7)
                            state <= ST_STOP;
                        else
                            bit_cnt <= bit_cnt + 3'd1;
                    end else begin
                        os_cnt <= os_cnt + 1'b1;
                    end
                end

                // ------------------------------------------------
                // Centro do stop bit. Se = 1, byte valido -> pulso wr.
                // OBS: o Terminal do Digital trata tanto CR (0x0D) quanto
                // LF (0x0A) como quebra de linha. Enviar "\r\n" pularia
                // DUAS linhas. Por isso suprimimos o CR aqui: o pulso 'wr'
                // nao e gerado para 0x0D, deixando apenas o LF quebrar a
                // linha. (Se preferir manter o CR, remova o teste != 8'h0D.)
                ST_STOP: begin
                    if (os_cnt == (OVS - 1)) begin
                        os_cnt <= 0;
                        if (rx_sync == 1'b1 && shreg != 8'h0D) begin
                            data <= shreg;  // byte pronto
                            wr   <= 1'b1;   // pulso para o Terminal
                        end
                        state <= ST_IDLE;
                    end else begin
                        os_cnt <= os_cnt + 1'b1;
                    end
                end

                default: state <= ST_IDLE;
            endcase
        end
    end

endmodule
*/

/* Code of uart_tx:
// ============================================================
// uart_tx_kbd.v  -  Transmissor UART 8N1 acoplado ao Keyboard
// ------------------------------------------------------------
// Variante do uart_tx.v com interface direta ao componente
// "Keyboard" do Digital (Neemann), que expoe:
//     D  (saida)  - byte disponivel
//     AV (saida)  - 1 quando ha byte na fila
//     Clock (ent) - borda de subida avanca para o proximo byte
//     Enable(ent) - habilita
//
// Ligacao no Digital:
//     Keyboard.D     -> uart_tx_kbd.data[7:0]
//     Keyboard.AV    -> uart_tx_kbd.av
//     uart_tx_kbd.next -> Keyboard.Clock   (pulso 1 ciclo, avanca fila)
//     Keyboard.Enable -> fixe em 1
//     uart_tx_kbd.tx -> uart_rx.rx         (linha serial)
//
// Cadeia completa dentro do Digital:
//     Keyboard -> uart_tx_kbd -> uart_rx -> Terminal
//
// Timing: cada bit dura OVS = CLK_FREQ / BAUD bordas de 'clk'.
//     Ex.: CLK_FREQ = 1600, BAUD = 100 -> OVS = 16 -> 10 bps.
// Frame: 1 start (0), 8 dados LSB-first, 1 stop (1). Sem paridade.
// Linha em repouso (idle) = 1.
// ============================================================

module uart_tx #(
    parameter CLK_FREQ = 1600,   // frequencia de 'clk' (Hz)
    parameter BAUD     = 100     // baud rate (bps)
) (
    input  wire       clk,      // clock de sistema (CLK_FREQ Hz)
    input  wire       rst_n,    // reset sincrono, ativo em 0 (logica negativa)
    input  wire [7:0] data,     // <- Keyboard.D
    input  wire       av,       // <- Keyboard.AV (1 = ha byte disponivel)
    output reg        next,     // -> Keyboard.Clock (pulso: avanca a fila)
    output reg        tx,       // -> linha serial (idle = 1)
    output reg        busy      // 1 enquanto transmite
);

    localparam OVS = CLK_FREQ / BAUD;

    localparam ST_IDLE  = 2'd0;
    localparam ST_START = 2'd1;
    localparam ST_DATA  = 2'd2;
    localparam ST_STOP  = 2'd3;

    reg [1:0] state;
    reg [$clog2(OVS)-1:0] os_cnt;
    reg [2:0] bit_cnt;
    reg [7:0] shreg;

    wire tick = (os_cnt == (OVS - 1));

    always @(posedge clk) begin
        if (!rst_n) begin
            state   <= ST_IDLE;
            os_cnt  <= 0;
            bit_cnt <= 3'd0;
            shreg   <= 8'd0;
            tx      <= 1'b1;
            busy    <= 1'b0;
            next    <= 1'b0;
        end else begin
            next <= 1'b0;   // pulso de avanco por padrao baixo

            case (state)
                // ------------------------------------------------
                // Ocioso: se o Keyboard tem byte (av=1), captura-o,
                // pulsa 'next' para avancar a fila e inicia o envio.
                ST_IDLE: begin
                    tx      <= 1'b1;
                    busy    <= 1'b0;
                    os_cnt  <= 0;
                    bit_cnt <= 3'd0;
                    if (av) begin
                        shreg <= data;    // captura o byte atual
                        next  <= 1'b1;    // avanca o Keyboard (1 ciclo)
                        busy  <= 1'b1;
                        tx    <= 1'b0;    // start bit
                        state <= ST_START;
                    end
                end

                // ------------------------------------------------
                ST_START: begin
                    if (tick) begin
                        os_cnt <= 0;
                        tx     <= shreg[0];
                        state  <= ST_DATA;
                    end else begin
                        os_cnt <= os_cnt + 1'b1;
                    end
                end

                // ------------------------------------------------
                ST_DATA: begin
                    if (tick) begin
                        os_cnt <= 0;
                        if (bit_cnt == 3'd7) begin
                            tx    <= 1'b1;
                            state <= ST_STOP;
                        end else begin
                            shreg   <= {1'b0, shreg[7:1]};
                            tx      <= shreg[1];
                            bit_cnt <= bit_cnt + 3'd1;
                        end
                    end else begin
                        os_cnt <= os_cnt + 1'b1;
                    end
                end

                // ------------------------------------------------
                ST_STOP: begin
                    if (tick) begin
                        os_cnt <= 0;
                        busy   <= 1'b0;
                        state  <= ST_IDLE;
                    end else begin
                        os_cnt <= os_cnt + 1'b1;
                    end
                end

                default: state <= ST_IDLE;
            endcase
        end
    end

endmodule
*/
